# Fritzing sketch serial (saved by Fritzing 0.9.3b)
breadboards: 1

parts:
  Part1 = Arduino Mega 2560 (Rev3)
  R1 = Resistor [tolerance=±5% resistance=10k package=THT]
  AX-12A = Basic Servo
  IC1 = IC, DIP package, 20 pins [chip_label=74LS241]
  XL-320 = Basic Servo
  R2 = Resistor [tolerance=±5% resistance=10k package=THT]
  R3 = Resistor [tolerance=±5% resistance=10k package=THT]
  R4 = Resistor [tolerance=±5% resistance=10k package=THT]
  11_1V = Power plug
  7_4V = Power plug

nets:
  N1: Part1.D19/RX1, IC1.pin18, R2.Pin_0
  N2: Part1.D18/TX1, IC1.pin17
  N3: Part1.D17_PWM/RX2, R1.Pin_0, IC1.pin16
  N4: Part1.D16_PWM/TX2, IC1.pin15
  N5: Part1.5V, R1.Pin_1, IC1.pin20, R2.Pin_1, R3.Pin_0, R4.Pin_0
  N6: Part1.GND, IC1.pin10
  N7: Part1.D2_PWM, IC1.pin1, IC1.pin19
  GND: AX-12A.gnd, 11_1V.GND
  VCC: AX-12A.vcc, 11_1V.VCC
  N8: AX-12A.pulse, IC1.pin2, IC1.pin3, R3.Pin_1
  N9: IC1.pin4, IC1.pin5, XL-320.pulse, R4.Pin_1
  GND_2: XL-320.gnd, 7_4V.GND
  VCC_2: XL-320.vcc, 7_4V.VCC
